# Fritzing sketch CPE301_Assignment2 (saved by Fritzing 0.9.3b)
breadboards: 1

parts:
  U1 = atmega328 [package=dip]
  R1 = Resistor [tolerance=±5% resistance=220 package=THT]
  LED1 = smd LED [color="Red (633nm)" package="1206 [SMD]"]
  S1 = SWITCH-MOMENTARY-2 [package=tactile-pth-12mm]

nets:
  N1: U1.D2, R1.Pin_0, S1.2
  N2: U1.AVCC, S1.1
  N3: U1.A3, LED1.anode
  GND: R1.Pin_1, LED1.cathode
